# Fritzing sketch SodoDaunoi (saved by Fritzing 0.9.9b)

parts:
  Part1 = Arduino Nano (Rev3.0)
  S1 = H-Bridge with L298N
  VCC1 = Battery
  Part2 = Bluetooth HC-05 Macho
  M1 = gear-motor
  M2 = gear-motor

nets:
  GND: Part1.GND, S1.GND, S1.M2-01, VCC1.-, Part2.GND, M1.pin_2
  N1: Part1.D2, Part2.TXD
  N2: Part1.D3, Part2.RXD
  N3: Part1.D6, S1.IN4
  N4: Part1.D7, S1.IN3
  N5: Part1.D8, S1.IN2
  N6: Part1.D9, S1.IN1
  VIN: Part1.VIN, S1.12V, VCC1.+
  5V: S1.5V, Part2.VCC
  N7: S1.M1-01, M2.pin_2
  N8: S1.M1-02, M2.pin_1
  N9: S1.M2-02, M1.pin_1

custom parts:
  H-Bridge with L298N: h-bridge
